# Fritzing sketch Control Remoto IR (saved by Fritzing 0.9.10b)
breadboards: 2

parts:
  Componente1 = Arduino Nano (Rev3.0)
  S1 = Pushbutton [package="[THT]"]
  S2 = Pushbutton [package="[THT]"]
  S3 = Pushbutton [package="[THT]"]
  S4 = Pushbutton [package="[THT]"]
  S5 = Pushbutton [package="[THT]"]
  BAT1 = 18650 battery holder [package=battery-18650-kit]
  BAT2 = 18650 battery holder [package=battery-18650-kit]
  R1 = Resistor [tolerance=±5% power=0.25 resistance=330 package=THT]
  LED1 = LED - 5mm [color="Red (633nm)" current=0.030 package="5 mm [THT]"]
  LED2 = LED - 5mm [color="Infrared (850nm)" current=0.030 package="5 mm [THT]"]
  R2 = Resistor [tolerance=±5% power=0.25 resistance=100 package=THT]
  Componente2 = Arduino Uno (Rev3)
  IR1 = TSOP312.., 314.. [package=THT]

nets:
  N1: Componente1.GND, Componente1.D2, S1.Pin_1, S1.Pin_2, S2.Pin_1, S2.Pin_2, S3.Pin_1, S3.Pin_2, S4.Pin_1, S4.Pin_2, S5.Pin_1, S5.Pin_2, BAT2.-, LED1.cathode, LED2.cathode
  N2: Componente1.D3, R1.Pin_0, R2.Pin_0
  N3: Componente1.VIN, BAT1.+
  N4: Componente1.A4, S5.Pin_3, S5.Pin_4
  N5: Componente1.A3, S4.Pin_3, S4.Pin_4
  N6: Componente1.A2, S3.Pin_3, S3.Pin_4
  N7: Componente1.A1, S2.Pin_3, S2.Pin_4
  N8: S1.Pin_3, S1.Pin_4
  N9: BAT1.-, BAT2.+
  N10: R1.Pin_1, LED1.anode
  N11: LED2.anode, R2.Pin_1
  N12: Componente2.D11_PWM/MOSI, IR1.Data
  GND: Componente2.GND, IR1.GND
  N13: Componente2.5V, IR1.Vs

custom parts:
  18650 battery holder: 18650 Battery Holder
